// Digital circuit UTS NO.1.dig as structural Verilog
module UTS_NO_1 (
  input  A,
  input  B,
  input  C
);

  wire and_1_out, and_2_out, and_3_out, and_4_out, and_5_out, not_1_out, or_1_out, or_2_out, or_3_out;

  and and_1 (and_1_out, A, B);
  and and_2 (and_2_out, B, C);
  and and_3 (and_3_out, C, A);
  or or_1 (or_1_out, A, B, C);
  and and_4 (and_4_out, A, B, C);
  or or_2 (or_2_out, and_1_out, and_2_out, and_3_out);
  not not_1 (not_1_out, or_2_out);
  and and_5 (and_5_out, not_1_out, or_1_out);
  or or_3 (or_3_out, and_5_out, and_4_out);
  LED X (.in(or_3_out));

  // Notes on the sheet:
  //   MUHAMMAD HIROKI 213050008
  //   1. (AB + AC + BC)' (A + B + C) + ABC
endmodule
