// Digital circuit UTS NO.12.dig as structural Verilog
module UTS_NO_12 (
  input  X,
  input  Y,
  input  Z,
  output P
);

  wire and_1_out, and_2_out, and_3_out, not_1_out;

  not not_1 (not_1_out, Y);
  not not_2 (not_1_out, Z);
  and and_1 (and_1_out, X, Y, not_1_out);
  and and_2 (and_2_out, X, Z);
  and and_3 (and_3_out, not_1_out, not_1_out);
  or or_1 (P, and_1_out, and_2_out, and_3_out);

  // Notes on the sheet:
  //   MUHAMMAD HIROKI 213050008
  //   12.XYZ' + Y'Z' +XZ
endmodule
