// Digital circuit UTS NO.15.dig as structural Verilog
module UTS_NO_15 (
  input  A,
  input  B,
  input  C,
  input  D
);

  wire and_1_out, and_2_out, and_3_out, and_4_out, not_1_out, not_2_out, not_3_out, not_4_out, not_5_out,
       not_6_out, or_1_out;

  not not_1 (not_1_out, C);
  not not_2 (not_2_out, C);
  not not_3 (not_3_out, A);
  not not_4 (not_4_out, D);
  not not_5 (not_5_out, B);
  not not_6 (not_6_out, D);
  and and_1 (and_1_out, A, B, not_1_out);
  and and_2 (and_2_out, not_2_out, D);
  and and_3 (and_3_out, not_3_out, C, not_4_out);
  and and_4 (and_4_out, not_5_out, C, not_6_out);
  or or_1 (or_1_out, and_1_out, and_2_out, and_3_out, and_4_out);
  LED R (.in(or_1_out));

  // Notes on the sheet:
  //   15. abc ' + c' d + a  ' cd ' +b ' cd '
  //   MUHAMMAD HIROKI 213050008
endmodule
